# Fritzing sketch schematic (saved by Fritzing 0.9.3b)
circuit board: 15.3004cm x 9.65106cm
breadboards: 1

parts:
  A = female pin header, 1 pin [form="♀ (female)"]
  C4 = Electrolytic Capacitor [capacitance=10µF package="100 mil [THT, electrolytic]"]
  SW = female pin header, 1 pin [form="♀ (female)"]
  TX = female pin header, 1 pin [form="♀ (female)"]
  USB = female pin header, 1 pin [form="♀ (female)"]
  +8V = female pin header, 1 pin [form="♀ (female)"]
  CONFIG = female pin header, 1 pin [form="♀ (female)"]
  C3 = Electrolytic Capacitor [capacitance=10µF package="100 mil [THT, electrolytic]"]
  LSB = female pin header, 1 pin [form="♀ (female)"]
  FI = female pin header, 1 pin [form="♀ (female)"]
  S-METER = female pin header, 1 pin [form="♀ (female)"]
  GND = female pin header, 1 pin [form="♀ (female)"]
  SI5351 = Adafruit Si5351A Clock Generator [part_number="Adafruit #2045"]
  INCREMENT = female pin header, 1 pin [form="♀ (female)"]
  U2 = SWITCH-SPST-2 [package=switch-spst-vertical]
  ROTARY_ENCODER1_WITh_BUTTON = Rotary Encoder with Knob
  COARSE_(20K)1 = POT [package=pot_mammoth]
  U3 = SWITCH-SPST-2 [package=switch-spst-vertical]
  B = female pin header, 1 pin [form="♀ (female)"]
  FM = female pin header, 1 pin [form="♀ (female)"]
  VFO = female pin header, 1 pin [form="♀ (female)"]
  AM = female pin header, 1 pin [form="♀ (female)"]
  CW = female pin header, 1 pin [form="♀ (female)"]
  SCL2 = female pin header, 1 pin [form="♀ (female)"]
  SDA1 = female pin header, 1 pin [form="♀ (female)"]
  FINE_(1K)1 = POT [package=pot_mammoth]
  C5 = Electrolytic Capacitor [capacitance=10µF package="100 mil [THT, electrolytic]"]
  C6 = Ceramic Capacitor [capacitance=100nF package="100 mil [THT, multilayer]"]
  L1 = Inductor [inductance=100µH package="1206 [SMD]"]
  R9 = Resistor [tolerance=±5% resistance=10k package="1206 [SMD]"]
  R11 = Resistor [tolerance=±5% resistance=10k package="1206 [SMD]"]
  R1 = Resistor [tolerance=±5% resistance=10k package="1206 [SMD]"]
  R6 = Resistor [tolerance=±5% resistance=680k package="1206 [SMD]"]
  R5 = Resistor [tolerance=±5% resistance=10k package="1206 [SMD]"]
  R4 = Resistor [tolerance=±5% resistance=10k package="1206 [SMD]"]
  R3 = Resistor [tolerance=±5% resistance=10k package="1206 [SMD]"]
  R2 = Resistor [tolerance=±5% resistance=10k package="1206 [SMD]"]
  R7 = Resistor [tolerance=±5% resistance=100k package="1206 [SMD]"]
  OLED_0_96 = Grove OLED 128x96
  R10 = Resistor [tolerance=±5% resistance=10k package="1206 [SMD]"]
  R12 = Resistor [tolerance=±5% resistance=10k package="1206 [SMD]"]
  R13 = Resistor [tolerance=±5% resistance=10k package="1206 [SMD]"]
  Arduino_Nano_-_µc = Arduino Nano (Rev3.0)
  GND_2 = female pin header, 1 pin [form="♀ (female)"]
  GND_3 = female pin header, 1 pin [form="♀ (female)"]
  +5V = female pin header, 1 pin [form="♀ (female)"]
  +5V_2 = female pin header, 1 pin [form="♀ (female)"]
  +5V_3 = female pin header, 1 pin [form="♀ (female)"]
  FREE = female pin header, 1 pin [form="♀ (female)"]
  SCL1 = female pin header, 1 pin [form="♀ (female)"]
  SDA2 = female pin header, 1 pin [form="♀ (female)"]

nets:
  N1: A.pin1, ROTARY_ENCODER1_WITh_BUTTON.no_name_yet#1, Arduino_Nano_-_µc.D3
  GND: C4.-, C3.-, GND.pin1, SI5351.GND, U2.O, ROTARY_ENCODER1_WITh_BUTTON.no_name_yet#3, ROTARY_ENCODER1_WITh_BUTTON.no_name_yet#4, COARSE_(20K)1.A, U3.O, C5.-, C6.0, R9.Pin_0, R11.Pin_0, OLED_0_96.GND, R10.Pin_0, R12.Pin_0, R13.Pin_0, Arduino_Nano_-_µc.GND, GND_2.pin1, GND_3.pin1
  N2: C4.+, L1.pin_0, OLED_0_96.VCC
  N3: SW.pin1, ROTARY_ENCODER1_WITh_BUTTON.no_name_yet#5, Arduino_Nano_-_µc.D4
  N4: TX.pin1, U3.P, Arduino_Nano_-_µc.D5
  N5: USB.pin1, R2.Pin_1
  N6: +8V.pin1, Arduino_Nano_-_µc.VIN
  N7: CONFIG.pin1, U2.P, Arduino_Nano_-_µc.D6
  5V: C3.+, SI5351.VIN, FINE_(1K)1.E, C5.+, C6.1, L1.pin_1, Arduino_Nano_-_µc.5V, +5V.pin1, +5V_2.pin1, +5V_3.pin1
  N8: LSB.pin1, R1.Pin_1
  N9: FI.pin1, SI5351.CLK0
  N10: S-METER.pin1, R6.Pin_0
  N11: SI5351.SDA, SDA1.pin1, OLED_0_96.SCL, Arduino_Nano_-_µc.A4, SDA2.pin1
  N12: SI5351.SCL, SCL2.pin1, OLED_0_96.SDA, Arduino_Nano_-_µc.A5, SCL1.pin1
  N13: SI5351.CLK2, VFO.pin1
  N14: INCREMENT.pin1, Arduino_Nano_-_µc.A1
  N15: ROTARY_ENCODER1_WITh_BUTTON.no_name_yet#2, B.pin1, Arduino_Nano_-_µc.D2
  CLARIFIER: COARSE_(20K)1.S, R7.Pin_0
  N16: COARSE_(20K)1.E, FINE_(1K)1.S, FINE_(1K)1.A
  N17: FM.pin1, R3.Pin_1
  N18: AM.pin1, R4.Pin_1
  N19: CW.pin1, R5.Pin_1
  N20: R9.Pin_1, R5.Pin_0, Arduino_Nano_-_µc.D12/MISO
  N21: R11.Pin_1, R3.Pin_0, Arduino_Nano_-_µc.D10
  N22: R1.Pin_0, R13.Pin_1, Arduino_Nano_-_µc.D8
  N23: R6.Pin_1, Arduino_Nano_-_µc.A3
  N24: R4.Pin_0, R10.Pin_1, Arduino_Nano_-_µc.D11/MOSI
  N25: R2.Pin_0, R12.Pin_1, Arduino_Nano_-_µc.D9
  N26: R7.Pin_1, Arduino_Nano_-_µc.A2
  N27: Arduino_Nano_-_µc.D7, FREE.pin1

notes:
  Vincent Hervieux - 14KM3506 - F4IQH
  On a Superstar 360 FM:
  Fi output connected to TR30 base - Quartz X4 removed
  VFO output connected to C107 in place of the TR26 emitter (TR26 removed)
  CLK0
  2022
  GND
  CLK2
  5V
  SCL
  Vincent Hervieux - 14KM3506
  JLCJLCJLCJLC
  https://gitlab.com/croutor/arduino-cibi-vfo
  CLK1
  SDA
  SI5351 DC filter
  OLED DC filter

custom parts:
  Adafruit Si5351A Clock Generator: Never hunt around for another crystal again, with the Si5351A clock generator breakout from Adafruit! This chip has a precision 25MHz crystal reference and internal PLL and dividers so it can generate just about any frequency, from <8KHz up to 150+ MHz. The Si5351A clock generator is an I2C controller clock generator. It uses the onboard precision clock to drive multiple PLL's and clock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
  Rotary Encoder with Knob: Rotary Encoder with 1/4" Shaft and Knob
